// Logisim project Lab4.circ as structural Verilog: 8 circuits, main circuit main
module main (
);

  ALU_Control alu_control_1 ();  // open: ALU_Ctrl1, ALU_Ctrl0, ALU_Src, ALU_Ctrl3, ALU_Ctrl2, I13, I12, I6, I5, I30, I4, I14
endmodule

module ALU_Control (
  input  I30,
  input  I14,
  input  I13,
  input  I12,
  input  I6,
  input  I5,
  input  I4,
  output ALU_Ctrl3,
  output ALU_Ctrl2,
  output ALU_Ctrl1,
  output ALU_Ctrl0,
  output ALU_Src
);

  wire and_2_out, not_1_out, not_2_out, not_3_out, not_4_out, not_5_out, not_6_out, not_7_out;

  not not_1 (not_1_out, I13);
  not not_2 (not_2_out, I13);
  not not_3 (not_3_out, I4);
  not not_4 (not_4_out, I12);
  not not_5 (not_5_out, I5);
  not not_6 (not_6_out, I4);
  and and_1 (ALU_Ctrl2, I30, not_1_out, I5);
  or or_1 (ALU_Ctrl1, not_2_out, not_3_out);
  not not_7 (not_7_out, I14);
  and and_2 (and_2_out, I13, not_4_out);
  or or_2 (ALU_Src, not_5_out, not_6_out);
  or or_3 (ALU_Ctrl0, not_7_out, and_2_out);

  assign ALU_Ctrl3 = 1'b0;
endmodule

module L_1_bit_Adder_a8395dc3 (
  input  A,
  input  B,
  input  C_in,
  output S,
  output C_out
);

  wire and_1_out, and_2_out, xor_1_out;

  xor xor_1 (xor_1_out, A, B);
  xor xor_2 (S, xor_1_out, C_in);
  and and_1 (and_1_out, xor_1_out, C_in);
  and and_2 (and_2_out, A, B);
  or or_1 (C_out, and_1_out, and_2_out);
endmodule

module OneBitALU (
  input  [3:0] ALU_Ctrl,
  input  A,
  input  B,
  input  C_in,
  output R,
  output out_6
);

  wire and_1_out, l_1_bit_adder_a8395dc3_1_s, multiplexer_1_out, not_1_out, or_1_out, xor_1_out;

  not not_1 (not_1_out, B);
  Multiplexer #(.enable("false")) multiplexer_1 (.in0(B), .in1(not_1_out), .out(multiplexer_1_out), .sel(ALU_Ctrl[2]));
  and and_1 (and_1_out, A, multiplexer_1_out);
  or or_1 (or_1_out, A, multiplexer_1_out);
  xor xor_1 (xor_1_out, A, multiplexer_1_out);
  L_1_bit_Adder_a8395dc3 l_1_bit_adder_a8395dc3_1 (
    .A(A), .B(multiplexer_1_out), .C_in(C_in), .S(l_1_bit_adder_a8395dc3_1_s), .C_out(out_6));
  Multiplexer #(.enable("false"), .select(2)) multiplexer_2 (
    .in0(and_1_out), .in1(or_1_out), .in2(xor_1_out), .in3(l_1_bit_adder_a8395dc3_1_s), .out(R),
    .sel(ALU_Ctrl[1:0]));
endmodule

module FourBitALU (
  input  C_in,
  input  [3:0] ALU_Ctrl,
  input  [3:0] A,
  input  [3:0] B,
  output [3:0] Result,
  output O
);

  wire onebitalu_1_out_6, onebitalu_2_out_6, onebitalu_3_out_6;

  OneBitALU onebitalu_1 (
    .ALU_Ctrl(ALU_Ctrl), .A(A[0]), .B(B[0]), .C_in(C_in), .R(Result[0]), .out_6(onebitalu_1_out_6));
  OneBitALU onebitalu_2 (
    .ALU_Ctrl(ALU_Ctrl), .A(A[1]), .B(B[1]), .C_in(onebitalu_1_out_6), .R(Result[1]),
    .out_6(onebitalu_2_out_6));
  OneBitALU onebitalu_3 (
    .ALU_Ctrl(ALU_Ctrl), .A(A[2]), .B(B[2]), .C_in(onebitalu_2_out_6), .R(Result[2]),
    .out_6(onebitalu_3_out_6));
  OneBitALU onebitalu_4 (.ALU_Ctrl(ALU_Ctrl), .A(A[3]), .B(B[3]), .C_in(onebitalu_3_out_6), .R(Result[3]), .out_6(O));
endmodule

module ThirtyTwoBitALU (
  input  [3:0] ALU_Ctrl,
  input  [31:0] A,
  input  [31:0] B,
  output [31:0] Result,
  output C_out
);

  wire fourbitalu_1_o, fourbitalu_2_o, fourbitalu_3_o, fourbitalu_4_o, fourbitalu_5_o, fourbitalu_6_o,
       fourbitalu_7_o;

  FourBitALU fourbitalu_1 (
    .C_in(ALU_Ctrl[2]), .ALU_Ctrl(ALU_Ctrl), .A(A[3:0]), .B(B[3:0]), .Result(Result[3:0]), .O(fourbitalu_1_o));
  FourBitALU fourbitalu_2 (
    .C_in(fourbitalu_1_o), .ALU_Ctrl(ALU_Ctrl), .A(A[7:4]), .B(B[7:4]), .Result(Result[7:4]),
    .O(fourbitalu_2_o));
  FourBitALU fourbitalu_3 (
    .C_in(fourbitalu_2_o), .ALU_Ctrl(ALU_Ctrl), .A(A[11:8]), .B(B[11:8]), .Result(Result[11:8]),
    .O(fourbitalu_3_o));
  FourBitALU fourbitalu_4 (
    .C_in(fourbitalu_3_o), .ALU_Ctrl(ALU_Ctrl), .A(A[15:12]), .B(B[15:12]), .Result(Result[15:12]),
    .O(fourbitalu_4_o));
  FourBitALU fourbitalu_5 (
    .C_in(fourbitalu_4_o), .ALU_Ctrl(ALU_Ctrl), .A(A[19:16]), .B(B[19:16]), .Result(Result[19:16]),
    .O(fourbitalu_5_o));
  FourBitALU fourbitalu_6 (
    .C_in(fourbitalu_5_o), .ALU_Ctrl(B[19:16]), .A(A[23:20]), .B(B[23:20]), .Result(Result[23:20]),
    .O(fourbitalu_6_o));
  FourBitALU fourbitalu_7 (
    .C_in(fourbitalu_6_o), .ALU_Ctrl(B[19:16]), .A(A[27:24]), .B(B[27:24]), .Result(Result[27:24]),
    .O(fourbitalu_7_o));
  FourBitALU fourbitalu_8 (
    .C_in(fourbitalu_7_o), .ALU_Ctrl(B[19:16]), .A(A[31:28]), .B(B[31:28]), .Result(Result[31:28]), .O(C_out));
endmodule

module ThirtyTwoRegister (
  input  [4:0] RReg1,
  input  [4:0] RReg2,
  input  [31:0] WriteData,
  input  [4:0] WriteReg,
  input  Write,
  input  Clock_In,
  output [31:0] RData1,
  output [31:0] RData2
);

  wire and_1_out, and_2_out, and_3_out, and_4_out, and_5_out, and_6_out, and_7_out, and_8_out, and_9_out,
       and_10_out, and_11_out, and_12_out, and_13_out, and_14_out, and_15_out, and_16_out, and_17_out,
       and_18_out, and_19_out, and_20_out, and_21_out, and_22_out, and_23_out, and_24_out, and_25_out,
       and_26_out, and_27_out, and_28_out, and_29_out, and_30_out, and_31_out, and_32_out, decoder_1_out0,
       decoder_1_out1, decoder_1_out2, decoder_1_out3, decoder_1_out4, decoder_1_out5, decoder_1_out6,
       decoder_1_out7, decoder_1_out8, decoder_1_out9, decoder_1_out10, decoder_1_out11, decoder_1_out12,
       decoder_1_out13, decoder_1_out14, decoder_1_out15, decoder_1_out16, decoder_1_out17, decoder_1_out18,
       decoder_1_out19, decoder_1_out20, decoder_1_out21, decoder_1_out22, decoder_1_out23, decoder_1_out24,
       decoder_1_out25, decoder_1_out26, decoder_1_out27, decoder_1_out28, decoder_1_out29, decoder_1_out30,
       decoder_1_out31;
  wire [31:0] register_1_q, register_2_q, register_3_q, register_4_q, register_5_q, register_6_q,
       register_7_q, register_8_q, register_9_q, register_10_q, register_11_q, register_12_q, register_13_q,
       register_14_q, register_15_q, register_16_q, register_17_q, register_18_q, register_19_q,
       register_20_q, register_21_q, register_22_q, register_23_q, register_24_q, register_25_q,
       register_26_q, register_27_q, register_28_q, register_29_q, register_30_q, register_31_q,
       register_32_q;

  Decoder #(.select(5)) decoder_1 (
    .out0(decoder_1_out0), .out1(decoder_1_out1), .out2(decoder_1_out2), .out3(decoder_1_out3),
    .out4(decoder_1_out4), .out5(decoder_1_out5), .out6(decoder_1_out6), .out7(decoder_1_out7),
    .out8(decoder_1_out8), .out9(decoder_1_out9), .out10(decoder_1_out10), .out11(decoder_1_out11),
    .out12(decoder_1_out12), .out13(decoder_1_out13), .out14(decoder_1_out14), .out15(decoder_1_out15),
    .out16(decoder_1_out16), .out17(decoder_1_out17), .out18(decoder_1_out18), .out19(decoder_1_out19),
    .out20(decoder_1_out20), .out21(decoder_1_out21), .out22(decoder_1_out22), .out23(decoder_1_out23),
    .out24(decoder_1_out24), .out25(decoder_1_out25), .out26(decoder_1_out26), .out27(decoder_1_out27),
    .out28(decoder_1_out28), .out29(decoder_1_out29), .out30(decoder_1_out30), .out31(decoder_1_out31),
    .sel(WriteReg));  // open: en
  and and_1 (and_1_out, decoder_1_out0, Write);
  and and_2 (and_2_out, decoder_1_out1, Write);
  and and_3 (and_3_out, decoder_1_out2, Write);
  and and_4 (and_4_out, decoder_1_out3, Write);
  and and_5 (and_5_out, decoder_1_out4, Write);
  and and_6 (and_6_out, decoder_1_out5, Write);
  and and_7 (and_7_out, decoder_1_out6, Write);
  and and_8 (and_8_out, decoder_1_out7, Write);
  Register #(.width(32)) register_1 (.D(WriteData), .clk(Clock_In), .Q(register_1_q), .clr(and_4_out));  // open: en
  Register #(.width(32)) register_2 (.D(WriteData), .clk(Clock_In), .Q(register_2_q), .clr(and_1_out));  // open: en
  Register #(.width(32)) register_3 (.D(WriteData), .clk(Clock_In), .Q(register_3_q), .clr(and_2_out));  // open: en
  Register #(.width(32)) register_4 (.D(WriteData), .clk(Clock_In), .Q(register_4_q), .clr(and_3_out));  // open: en
  Register #(.width(32)) register_5 (.D(WriteData), .clk(Clock_In), .Q(register_5_q), .clr(and_5_out));  // open: en
  Register #(.width(32)) register_6 (.D(WriteData), .clk(Clock_In), .Q(register_6_q), .clr(and_6_out));  // open: en
  Register #(.width(32)) register_7 (.D(WriteData), .clk(Clock_In), .Q(register_7_q), .clr(and_7_out));  // open: en
  Register #(.width(32)) register_8 (.D(WriteData), .clk(Clock_In), .Q(register_8_q), .clr(and_8_out));  // open: en
  and and_9 (and_9_out, decoder_1_out8, Write);
  and and_10 (and_10_out, decoder_1_out9, Write);
  and and_11 (and_11_out, decoder_1_out10, Write);
  and and_12 (and_12_out, decoder_1_out11, Write);
  and and_13 (and_13_out, decoder_1_out12, Write);
  and and_14 (and_14_out, decoder_1_out13, Write);
  and and_15 (and_15_out, decoder_1_out14, Write);
  and and_16 (and_16_out, decoder_1_out15, Write);
  Register #(.width(32)) register_9 (.D(WriteData), .clk(Clock_In), .Q(register_9_q), .clr(and_9_out));  // open: en
  Register #(.width(32)) register_10 (.D(WriteData), .clk(Clock_In), .Q(register_10_q), .clr(and_10_out));  // open: en
  Register #(.width(32)) register_11 (.D(WriteData), .clk(Clock_In), .Q(register_11_q), .clr(and_11_out));  // open: en
  Register #(.width(32)) register_12 (.D(WriteData), .clk(Clock_In), .Q(register_12_q), .clr(and_12_out));  // open: en
  Register #(.width(32)) register_13 (.D(WriteData), .clk(Clock_In), .Q(register_13_q), .clr(and_13_out));  // open: en
  Register #(.width(32)) register_14 (.D(WriteData), .clk(Clock_In), .Q(register_14_q), .clr(and_14_out));  // open: en
  Register #(.width(32)) register_15 (.D(WriteData), .clk(Clock_In), .Q(register_15_q), .clr(and_15_out));  // open: en
  Register #(.width(32)) register_16 (.D(WriteData), .clk(Clock_In), .Q(register_16_q), .clr(and_16_out));  // open: en
  and and_17 (and_17_out, decoder_1_out16, Write);
  and and_18 (and_18_out, decoder_1_out17, Write);
  and and_19 (and_19_out, decoder_1_out18, Write);
  and and_20 (and_20_out, decoder_1_out19, Write);
  and and_21 (and_21_out, decoder_1_out20, Write);
  and and_22 (and_22_out, decoder_1_out21, Write);
  and and_23 (and_23_out, decoder_1_out22, Write);
  and and_24 (and_24_out, decoder_1_out23, Write);
  Register #(.width(32)) register_17 (.D(WriteData), .clk(Clock_In), .Q(register_17_q), .clr(and_17_out));  // open: en
  Register #(.width(32)) register_18 (.D(WriteData), .clk(Clock_In), .Q(register_18_q), .clr(and_18_out));  // open: en
  Register #(.width(32)) register_19 (.D(WriteData), .clk(Clock_In), .Q(register_19_q), .clr(and_19_out));  // open: en
  Register #(.width(32)) register_20 (.D(WriteData), .clk(Clock_In), .Q(register_20_q), .clr(and_20_out));  // open: en
  Register #(.width(32)) register_21 (.D(WriteData), .clk(Clock_In), .Q(register_21_q), .clr(and_21_out));  // open: en
  Register #(.width(32)) register_22 (.D(WriteData), .clk(Clock_In), .Q(register_22_q), .clr(and_22_out));  // open: en
  Register #(.width(32)) register_23 (.D(WriteData), .clk(Clock_In), .Q(register_23_q), .clr(and_23_out));  // open: en
  Register #(.width(32)) register_24 (.D(WriteData), .clk(Clock_In), .Q(register_24_q), .clr(and_24_out));  // open: en
  and and_25 (and_25_out, decoder_1_out24, Write);
  and and_26 (and_26_out, decoder_1_out25, Write);
  and and_27 (and_27_out, decoder_1_out26, Write);
  and and_28 (and_28_out, decoder_1_out27, Write);
  and and_29 (and_29_out, decoder_1_out28, Write);
  and and_30 (and_30_out, decoder_1_out29, Write);
  and and_31 (and_31_out, decoder_1_out30, Write);
  and and_32 (and_32_out, decoder_1_out31, Write);
  Register #(.width(32)) register_25 (.D(WriteData), .clk(Clock_In), .Q(register_25_q), .clr(and_25_out));  // open: en
  Register #(.width(32)) register_26 (.D(WriteData), .clk(Clock_In), .Q(register_26_q), .clr(and_26_out));  // open: en
  Register #(.width(32)) register_27 (.D(WriteData), .clk(Clock_In), .Q(register_27_q), .clr(and_27_out));  // open: en
  Register #(.width(32)) register_28 (.D(WriteData), .clk(Clock_In), .Q(register_28_q), .clr(and_28_out));  // open: en
  Register #(.width(32)) register_29 (.D(WriteData), .clk(Clock_In), .Q(register_29_q), .clr(and_29_out));  // open: en
  Register #(.width(32)) register_30 (.D(WriteData), .clk(Clock_In), .Q(register_30_q), .clr(and_30_out));  // open: en
  Register #(.width(32)) register_31 (.D(WriteData), .clk(Clock_In), .Q(register_31_q), .clr(and_31_out));  // open: en
  Register #(.width(32)) register_32 (.D(WriteData), .clk(Clock_In), .Q(register_32_q), .clr(and_32_out));  // open: en
  Multiplexer #(.enable("false"), .select(5), .width(32)) multiplexer_1 (
    .in0(register_2_q), .in1(register_3_q), .in2(register_4_q), .in3(register_1_q), .in4(register_5_q),
    .in5(register_6_q), .in6(register_7_q), .in7(register_8_q), .in8(register_9_q), .in9(register_10_q),
    .in10(register_11_q), .in11(register_12_q), .in12(register_13_q), .in13(register_14_q),
    .in14(register_15_q), .in15(register_16_q), .in16(register_17_q), .in17(register_18_q),
    .in18(register_19_q), .in19(register_20_q), .in20(register_21_q), .in21(register_22_q),
    .in22(register_23_q), .in23(register_24_q), .in24(register_25_q), .in25(register_26_q),
    .in26(register_27_q), .in27(register_28_q), .in28(register_29_q), .in29(register_30_q),
    .in30(register_31_q), .in31(register_32_q), .out(RData1), .sel(RReg1));
  Multiplexer #(.enable("false"), .select(5), .width(32)) multiplexer_2 (
    .in0(register_2_q), .in1(register_3_q), .in2(register_4_q), .in3(register_1_q), .in4(register_5_q),
    .in5(register_6_q), .in6(register_7_q), .in7(register_8_q), .in8(register_9_q), .in9(register_10_q),
    .in10(register_11_q), .in11(register_12_q), .in12(register_13_q), .in13(register_14_q),
    .in14(register_15_q), .in15(register_16_q), .in16(register_17_q), .in17(register_18_q),
    .in18(register_19_q), .in19(register_20_q), .in20(register_21_q), .in21(register_22_q),
    .in22(register_23_q), .in23(register_24_q), .in24(register_25_q), .in25(register_26_q),
    .in26(register_27_q), .in27(register_28_q), .in28(register_29_q), .in29(register_30_q),
    .in30(register_31_q), .in31(register_32_q), .out(RData2), .sel(RReg2));
endmodule

module DataPath (
  input  [31:0] in_1
);

  wire alu_control_1_alu_src, clock_1_out;
  wire [3:0] alu_control_1_alu_ctrl0;
  wire [31:0] multiplexer_1_out, thirtytwobitalu_1_result, thirtytworegister_1_rdata1,
       thirtytworegister_1_rdata2;

  Clock clock_1 (.out(clock_1_out));
  Bit_Extender #(.in_width(12), .out_width(32)) bit_extender_1 (.in(in_1[31:20]));  // open: out
  ThirtyTwoRegister thirtytworegister_1 (
    .RReg1(in_1[19:15]), .RReg2(in_1[24:20]), .WriteData(thirtytwobitalu_1_result), .WriteReg(in_1[11:7]),
    .Write(1'b1), .Clock_In(clock_1_out), .RData1(thirtytworegister_1_rdata1),
    .RData2(thirtytworegister_1_rdata2));
  ALU_Control alu_control_1 (
    .ALU_Ctrl1(alu_control_1_alu_ctrl0[1]), .ALU_Ctrl0(alu_control_1_alu_ctrl0[0]),
    .ALU_Src(alu_control_1_alu_src), .ALU_Ctrl3(alu_control_1_alu_ctrl0[3]),
    .ALU_Ctrl2(alu_control_1_alu_ctrl0[2]), .I13(in_1[13]), .I12(in_1[12]), .I6(in_1[6]), .I5(in_1[5]),
    .I30(in_1[30]), .I4(in_1[4]), .I14(in_1[14]));
  Multiplexer #(.enable("false"), .width(32)) multiplexer_1 (
    .in0(thirtytworegister_1_rdata2), .out(multiplexer_1_out), .sel(alu_control_1_alu_src));  // open: in1
  ThirtyTwoBitALU thirtytwobitalu_1 (
    .ALU_Ctrl(alu_control_1_alu_ctrl0), .A(thirtytworegister_1_rdata1), .B(multiplexer_1_out),
    .Result(thirtytwobitalu_1_result));  // open: C_out
endmodule
